# Fritzing sketch Stepper Control Circuit (saved by Fritzing 0.9.4)
circuit board: 7cm x 7.4cm
breadboards: 1

parts:
  R1 = Resistor [tolerance=±5% resistance=1k package=THT]
  U1 = TLP621 [package=THT]
  R5 = Resistor [tolerance=±5% resistance=1k package=THT]
  U2 = TLP621 [package=THT]
  R6 = Resistor [tolerance=±5% resistance=1k package=THT]
  R8 = Resistor [tolerance=±5% resistance=10k package=THT]
  R9 = Resistor [tolerance=±5% resistance=1k package=THT]
  U3 = TLP621 [package=THT]
  R12 = Resistor [tolerance=±5% resistance=10k package=THT]
  R10 = Resistor [tolerance=±5% resistance=1k package=THT]
  U4 = TLP621 [package=THT]
  R13 = Resistor [tolerance=±5% resistance=1k package=THT]
  R14 = Resistor [tolerance=±5% resistance=1k package=THT]
  R16 = Resistor [tolerance=±5% resistance=10k package=THT]
  J1 = male pin header, 5 pins [form="♂ (male)"]
  R2 = Resistor [tolerance=±5% resistance=1k package=THT]
  J2 = male pin header, 2 pins [form="♂ (male)" part_number="24 VDC"]
  R4 = Resistor [tolerance=±5% resistance=10k package=THT]
  R17 = Resistor [tolerance=±5% resistance=1k package=THT]
  U5 = Voltage Regulator - 5V [package="TO220 [THT]"]
  D2 = Schottky Diode [part_number=1N5817 package="300 mil [THT]"]
  D1 = Schottky Diode [part_number=1N5817 package="300 mil [THT]"]
  R19 = Resistor [tolerance=±5% resistance=10 package=THT]
  D3 = Schottky Diode [part_number=1N5817 package="300 mil [THT]"]
  D4 = Schottky Diode [part_number=1N5817 package="300 mil [THT]"]
  R21 = Resistor [tolerance=±5% resistance=10 package=THT]
  J3 = male pin header, 4 pins [form="♂ (male)"]
  U7 = L6203 [package=multiwatt11]
  U6 = L6203 [package=multiwatt11]
  C9 = Ceramic Capacitor [capacitance=22nF package="200 mil [THT, multilayer]"]
  C7 = Ceramic Capacitor [capacitance=15nF package="200 mil [THT, multilayer]"]
  C8 = Ceramic Capacitor [capacitance=15nF package="200 mil [THT, multilayer]"]
  C6 = Ceramic Capacitor [capacitance=100nF package="200 mil [THT, multilayer]"]
  C4 = Ceramic Capacitor [capacitance=15nF package="200 mil [THT, multilayer]"]
  C3 = Ceramic Capacitor [capacitance=15nF package="200 mil [THT, multilayer]"]
  C5 = Ceramic Capacitor [capacitance=22nF package="200 mil [THT, multilayer]"]
  C1 = Ceramic Capacitor [capacitance=100nF package="200 mil [THT, multilayer]"]
  C2 = Ceramic Capacitor [capacitance=100nF package="200 mil [THT, multilayer]"]
  R22 = Resistor [tolerance=±5% resistance=10k package=THT]
  J4 = double row male pin header, 8 pins [form="♂ (male)"]
  R23 = Resistor [tolerance=±5% resistance=10k package=THT]
  R18 = Resistor [tolerance=±5% resistance=1 package=THT]
  R20 = Resistor [tolerance=±5% resistance=1 package=THT]

nets:
  N1: R1.Pin_0, J1.pin1
  N2: R1.Pin_1, U1.Pin_1
  N3: U1.Pin_2, U2.Pin_2, U3.Pin_2, U4.Pin_2, J1.pin5
  N4: U1.Pin_4, R2.Pin_1
  N5: U1.Pin_3, R4.Pin_0, U6.IN1
  N6: R5.Pin_0, J1.pin2
  N7: R5.Pin_1, U2.Pin_1
  N8: U2.Pin_4, R6.Pin_1
  N9: U2.Pin_3, R8.Pin_0, U6.IN2
  N10: R6.Pin_0, R10.Pin_0, R14.Pin_0, R2.Pin_0, R17.Pin_1, U5.output_voltage
  GND: R8.Pin_1, R12.Pin_1, R16.Pin_1, J2.pin2, R4.Pin_1, U5.GND, D2.anode, D1.anode, D3.anode, D4.anode, U7.GND, U6.GND, C6.0, C1.0, C2.1, R18.Pin_1, R20.Pin_1
  N11: R9.Pin_0, J1.pin3
  N12: R9.Pin_1, U3.Pin_1
  N13: U3.Pin_4, R10.Pin_1
  N14: U3.Pin_3, R12.Pin_0, U7.IN1
  N15: U4.Pin_1, R13.Pin_1
  N16: U4.Pin_4, R14.Pin_1
  N17: U4.Pin_3, R16.Pin_0, U7.IN2
  N18: R13.Pin_0, J1.pin4
  N19: J2.pin1, U5.input_voltage, U7.VS, U6.VS, C2.0
  N20: R17.Pin_0, U7.ENABLE, U6.ENABLE
  N21: D2.cathode, R19.Pin_0, J3.pin1, U6.OUT1, C3.0, R22.Pin_0
  N22: D1.cathode, J3.pin2, U6.OUT2, C4.1, C5.0, J4.pin2, J4.pin8
  N23: R19.Pin_1, C5.1
  N24: D3.cathode, J3.pin4, U7.OUT2, C9.0, C7.1, J4.pin3, J4.pin5
  N25: D4.cathode, R21.Pin_0, J3.pin3, U7.OUT1, C8.0, R23.Pin_0
  N26: R21.Pin_1, C9.1
  N27: U7.BOOT1, C8.1
  N28: U7.BOOT2, C7.0
  N29: U7.VREF, C6.1
  N30: U7.SENSE, R20.Pin_0
  N31: U6.BOOT1, C3.1
  N32: U6.BOOT2, C4.0
  N33: U6.VREF, C1.1
  N34: U6.SENSE, R18.Pin_0
  N35: R22.Pin_1, J4.pin1, J4.pin7
  N36: J4.pin4, J4.pin6, R23.Pin_1

notes:
  +VE
  GND
  1
  2
  3
  4
  Gary Twinn 2020
  Input
  Output
  RpI BiPolar Stepper Driver V1.2
  Channel LEDs
  +
  -
  Raspberry Pi

custom parts:
  L6203: L6203 Single Bridge Driver
